// Logisim project B86524-ALU.circ as structural Verilog: 1 circuit, main circuit ALU
module ALU (
  input  [31:0] A,
  input  [31:0] B,
  input  [3:0] AluOP,
  output Signed_Overflow,
  output UnSigned_Overflow,
  output Equal,
  output [31:0] Result,
  output [31:0] Result_2
);

  wire adder_1_cout, adder_2_cout, and_2_out, cin, comparator_3_gt, comparator_4_gt, subtractor_1_bout,
       xor_2_out;
  wire [0:0] comparator_1_lt, comparator_2_lt;
  wire [6:0] bitadder_1_out;
  wire [30:0] adder_1_out;
  wire [31:0] and_1_out, divider_1_out, divider_1_rem, divider_2_rem, multiplier_1_cout, multiplier_1_out,
       nand_1_out, nor_1_out, shifter_1_out, shifter_2_out, shifter_3_out, subtractor_1_out, xor_1_out;
  wire [31:31] adder_2_out;

  // Probe on A
  // Probe on A
  // Probe on B
  // Probe on B
  Adder #(.width(31)) adder_1 (.a(A[30:0]), .b(B[30:0]), .out(adder_1_out), .cin(cin), .cout(adder_1_cout));
  assign and_1_out = A & B;  // AND_Gate and_1, 32 bits wide
  assign and_1_out = A | B;  // OR_Gate or_1, 32 bits wide
  assign xor_1_out = A ^ B;  // XOR_Gate xor_1, 32 bits wide
  Shifter #(.width(32), .shift("lr")) shifter_1 (.in(A), .\dist (B[4:0]), .out(shifter_1_out));
  Shifter #(.width(32), .shift("ar")) shifter_2 (.in(A), .\dist (B[4:0]), .out(shifter_2_out));
  Comparator #(.width(32)) comparator_1 (.a(A), .b(B), .eq(Equal), .lt(comparator_1_lt[0]));  // open: gt
  Shifter #(.width(32)) shifter_3 (.in(A), .\dist (B[4:0]), .out(shifter_3_out));
  Comparator #(.width(32)) comparator_2 (.a(A), .b(B), .lt(comparator_2_lt[0]));  // open: gt, eq
  Divider #(.width(32)) divider_1 (.a(A), .b(B), .out(divider_1_out), .rem(divider_1_rem));  // open: upper
  Divider #(.width(32)) divider_2 (.a(A), .b(B), .rem(divider_2_rem));  // open: out, upper
  Multiplier #(.width(32)) multiplier_1 (.a(A), .b(B), .out(multiplier_1_out), .cout(multiplier_1_cout));  // open: cin
  Subtractor #(.width(32)) subtractor_1 (.a(A), .b(B), .out(subtractor_1_out), .bout(subtractor_1_bout));  // open: bin
  assign nand_1_out = ~(A & B);  // NAND_Gate nand_1, 32 bits wide
  assign nor_1_out = ~(A | B);  // NOR_Gate nor_1, 32 bits wide
  Adder #(.width(1)) adder_2 (.a(A[31]), .b(B[31]), .out(adder_2_out[31]), .cin(adder_1_cout), .cout(adder_2_cout));
  BitAdder #(.width(32)) bitadder_1 (.in0(A), .in1(B), .out(bitadder_1_out));
  // Probe on AluOP
  // Probe on Result
  // Probe on Result
  xor xor_2 (xor_2_out, adder_1_cout, adder_2_cout);
  Multiplexer #(.select(4), .width(32), .enable("false")) multiplexer_1 (
    .in0({adder_2_out[31], adder_1_out}), .in1(and_1_out), .in2(and_1_out), .in3(xor_1_out),
    .in4(shifter_1_out), .in5(shifter_2_out), .in6({{31{1'b0}}, comparator_1_lt[0]}), .in7(shifter_3_out),
    .in8({{31{1'b0}}, comparator_2_lt[0]}), .in9(divider_1_out), .in10(divider_2_rem),
    .in11(multiplier_1_out), .in12(subtractor_1_out), .in13({{25{1'b0}}, bitadder_1_out}), .in14(nand_1_out),
    .in15(nor_1_out), .out(Result), .sel(AluOP));
  // Probe on Result_2
  Multiplexer #(.select(4), .width(32), .enable("false")) multiplexer_2 (
    .in0({32{1'b0}}), .in1({32{1'b0}}), .in2({32{1'b0}}), .in3({32{1'b0}}), .in4({32{1'b0}}),
    .in5({32{1'b0}}), .in6({32{1'b0}}), .in7({32{1'b0}}), .in8(divider_1_rem), .in9({32{1'b0}}),
    .in10({32{1'b0}}), .in11(multiplier_1_cout), .in12({32{1'b0}}), .in13({32{1'b0}}), .in14({32{1'b0}}),
    .in15({32{1'b0}}), .out(Result_2), .sel(AluOP));
  Comparator #(.width(32)) comparator_3 (.a(multiplier_1_out), .b({32{1'b0}}), .gt(comparator_3_gt));  // open: eq, lt
  Comparator #(.width(32)) comparator_4 (.a(multiplier_1_cout), .b({32{1'b0}}), .gt(comparator_4_gt));  // open: eq, lt
  and and_2 (and_2_out, comparator_3_gt, comparator_4_gt);
  Multiplexer #(.select(4), .enable("false")) multiplexer_3 (
    .in0(adder_2_cout), .in1(1'b0), .in2(1'b0), .in3(1'b0), .in4(1'b0), .in5(1'b0), .in6(1'b0), .in7(1'b0),
    .in8(1'b0), .in9(1'b0), .in10(and_2_out), .in11(1'b0), .in12(1'b0), .in13(1'b0), .in14(1'b0),
    .in15(1'b0), .out(UnSigned_Overflow), .sel(AluOP));
  Multiplexer #(.select(4), .enable("false")) multiplexer_4 (
    .in0(xor_2_out), .in1(1'b0), .in2(1'b0), .in3(1'b0), .in4(1'b0), .in5(1'b0), .in6(1'b0), .in7(1'b0),
    .in8(1'b0), .in9(1'b0), .in10(1'b0), .in11(1'b0), .in12(subtractor_1_bout), .in13(1'b0), .in14(1'b0),
    .in15(1'b0), .out(Signed_Overflow), .sel(AluOP));

  // Other names for the same wires on the sheet: CF = UnSigned_Overflow; OF = Signed_Overflow;
  //   Result2[31:0] = Result_2; S[3:0] = AluOP

  // Notes on the sheet:
  //   ALU
  //   First input
  //   Decimal representations
  //   Second input
  //   Input pins
  //   Output pins
  //   Debug area
endmodule
