// Logisim project 32 bit Register File.circ as structural Verilog: 1 circuit, main circuit main
module main (
  input  [4:0] rd,
  input  [4:0] rs,
  input  [4:0] rt,
  output [31:0] crs,
  output [31:0] crd
);

  wire clock_1_out, demultiplexer_1_out0, demultiplexer_1_out1, demultiplexer_1_out2, demultiplexer_1_out3,
       demultiplexer_1_out4, demultiplexer_1_out5, demultiplexer_1_out6, demultiplexer_1_out7,
       demultiplexer_1_out8, demultiplexer_1_out9, demultiplexer_1_out10, demultiplexer_1_out11,
       demultiplexer_1_out12, demultiplexer_1_out13, demultiplexer_1_out14, demultiplexer_1_out15,
       demultiplexer_1_out16, demultiplexer_1_out17, demultiplexer_1_out18, demultiplexer_1_out19,
       demultiplexer_1_out20, demultiplexer_1_out21, demultiplexer_1_out22, demultiplexer_1_out23,
       demultiplexer_1_out24, demultiplexer_1_out25, demultiplexer_1_out26, demultiplexer_1_out27,
       demultiplexer_1_out28, demultiplexer_1_out29, demultiplexer_1_out30, demultiplexer_1_out31;
  wire [31:0] R0_q, R1_q, R2_q, R3_q, R4_q, R5_q, R6_q, R7_q, R8_q, R9_q, R10_q, R11_q, R12_q, R13_q, R14_q,
       R15_q, R16_q, R17_q, R18_q, R19_q, R20_q, R21_q, R22_q, R23_q, R24_q, R25_q, R26_q, R27_q, R28_q,
       R29_q, R30_q, R31_q;

  Demultiplexer #(.select(5), .enable("false")) demultiplexer_1 (
    .out0(demultiplexer_1_out0), .out1(demultiplexer_1_out1), .out2(demultiplexer_1_out2),
    .out3(demultiplexer_1_out3), .out4(demultiplexer_1_out4), .out5(demultiplexer_1_out5),
    .out6(demultiplexer_1_out6), .out7(demultiplexer_1_out7), .out8(demultiplexer_1_out8),
    .out9(demultiplexer_1_out9), .out10(demultiplexer_1_out10), .out11(demultiplexer_1_out11),
    .out12(demultiplexer_1_out12), .out13(demultiplexer_1_out13), .out14(demultiplexer_1_out14),
    .out15(demultiplexer_1_out15), .out16(demultiplexer_1_out16), .out17(demultiplexer_1_out17),
    .out18(demultiplexer_1_out18), .out19(demultiplexer_1_out19), .out20(demultiplexer_1_out20),
    .out21(demultiplexer_1_out21), .out22(demultiplexer_1_out22), .out23(demultiplexer_1_out23),
    .out24(demultiplexer_1_out24), .out25(demultiplexer_1_out25), .out26(demultiplexer_1_out26),
    .out27(demultiplexer_1_out27), .out28(demultiplexer_1_out28), .out29(demultiplexer_1_out29),
    .out30(demultiplexer_1_out30), .out31(demultiplexer_1_out31), .sel(rd));  // open: in
  Clock clock_1 (.out(clock_1_out));
  Register #(.width(32), .Select("low")) R0 (.Q(R0_q), .clk(clock_1_out), .clr(demultiplexer_1_out0));  // open: D, en
  Register #(.width(32), .Select("low")) R8 (.Q(R8_q), .clk(clock_1_out), .clr(demultiplexer_1_out8));  // open: D, en
  Register #(.width(32), .Select("low")) R16 (
    .Q(R16_q), .clk(clock_1_out), .clr(demultiplexer_1_out16));  // open: D, en
  Register #(.width(32), .Select("low")) R24 (
    .Q(R24_q), .clk(clock_1_out), .clr(demultiplexer_1_out24));  // open: D, en
  Register #(.width(32), .Select("low")) R2 (.Q(R2_q), .clk(clock_1_out), .clr(demultiplexer_1_out2));  // open: D, en
  Register #(.width(32), .Select("low")) R1 (.Q(R1_q), .clk(clock_1_out), .clr(demultiplexer_1_out1));  // open: D, en
  Register #(.width(32), .Select("low")) R10 (
    .Q(R10_q), .clk(clock_1_out), .clr(demultiplexer_1_out10));  // open: D, en
  Register #(.width(32), .Select("low")) R9 (.Q(R9_q), .clk(clock_1_out), .clr(demultiplexer_1_out9));  // open: D, en
  Register #(.width(32), .Select("low")) R18 (
    .Q(R18_q), .clk(clock_1_out), .clr(demultiplexer_1_out18));  // open: D, en
  Register #(.width(32), .Select("low")) R17 (
    .Q(R17_q), .clk(clock_1_out), .clr(demultiplexer_1_out17));  // open: D, en
  Register #(.width(32), .Select("low")) R26 (
    .Q(R26_q), .clk(clock_1_out), .clr(demultiplexer_1_out26));  // open: D, en
  Register #(.width(32), .Select("low")) R25 (
    .Q(R25_q), .clk(clock_1_out), .clr(demultiplexer_1_out25));  // open: D, en
  Register #(.width(32), .Select("low")) R3 (.Q(R3_q), .clk(clock_1_out), .clr(demultiplexer_1_out3));  // open: D, en
  Register #(.width(32), .Select("low")) R11 (
    .Q(R11_q), .clk(clock_1_out), .clr(demultiplexer_1_out11));  // open: D, en
  Register #(.width(32), .Select("low")) R19 (
    .Q(R19_q), .clk(clock_1_out), .clr(demultiplexer_1_out19));  // open: D, en
  Register #(.width(32), .Select("low")) R27 (
    .Q(R27_q), .clk(clock_1_out), .clr(demultiplexer_1_out27));  // open: D, en
  Register #(.width(32), .Select("low")) R4 (.Q(R4_q), .clk(clock_1_out), .clr(demultiplexer_1_out4));  // open: D, en
  Register #(.width(32), .Select("low")) R5 (.Q(R5_q), .clk(clock_1_out), .clr(demultiplexer_1_out5));  // open: D, en
  Register #(.width(32), .Select("low")) R12 (
    .Q(R12_q), .clk(clock_1_out), .clr(demultiplexer_1_out12));  // open: D, en
  Register #(.width(32), .Select("low")) R13 (
    .Q(R13_q), .clk(clock_1_out), .clr(demultiplexer_1_out13));  // open: D, en
  Register #(.width(32), .Select("low")) R20 (
    .Q(R20_q), .clk(clock_1_out), .clr(demultiplexer_1_out20));  // open: D, en
  Register #(.width(32), .Select("low")) R21 (
    .Q(R21_q), .clk(clock_1_out), .clr(demultiplexer_1_out21));  // open: D, en
  Register #(.width(32), .Select("low")) R28 (
    .Q(R28_q), .clk(clock_1_out), .clr(demultiplexer_1_out28));  // open: D, en
  Register #(.width(32), .Select("low")) R29 (
    .Q(R29_q), .clk(clock_1_out), .clr(demultiplexer_1_out29));  // open: D, en
  Register #(.width(32), .Select("low")) R6 (.Q(R6_q), .clk(clock_1_out), .clr(demultiplexer_1_out6));  // open: D, en
  Register #(.width(32), .Select("low")) R14 (
    .Q(R14_q), .clk(clock_1_out), .clr(demultiplexer_1_out14));  // open: D, en
  Register #(.width(32), .Select("low")) R22 (
    .Q(R22_q), .clk(clock_1_out), .clr(demultiplexer_1_out22));  // open: D, en
  Register #(.width(32), .Select("low")) R30 (
    .Q(R30_q), .clk(clock_1_out), .clr(demultiplexer_1_out30));  // open: D, en
  Register #(.width(32), .Select("low")) R7 (.Q(R7_q), .clk(clock_1_out), .clr(demultiplexer_1_out7));  // open: D, en
  Register #(.width(32), .Select("low")) R15 (
    .Q(R15_q), .clk(clock_1_out), .clr(demultiplexer_1_out15));  // open: D, en
  Register #(.width(32), .Select("low")) R23 (
    .Q(R23_q), .clk(clock_1_out), .clr(demultiplexer_1_out23));  // open: D, en
  Register #(.width(32), .Select("low")) R31 (
    .Q(R31_q), .clk(clock_1_out), .clr(demultiplexer_1_out31));  // open: D, en
  Multiplexer #(.select(5), .width(32), .enable("false")) multiplexer_1 (
    .in0(R0_q), .in1(R1_q), .in2(R2_q), .in3(R3_q), .in4(R4_q), .in5(R5_q), .in6(R6_q), .in7(R7_q),
    .in8(R8_q), .in9(R9_q), .in10(R10_q), .in11(R11_q), .in12(R12_q), .in13(R13_q), .in14(R14_q),
    .in15(R15_q), .in16(R16_q), .in17(R17_q), .in18(R18_q), .in19(R19_q), .in20(R20_q), .in21(R21_q),
    .in22(R22_q), .in23(R23_q), .in24(R24_q), .in25(R25_q), .in26(R26_q), .in27(R27_q), .in28(R28_q),
    .in29(R29_q), .in30(R30_q), .in31(R31_q), .out(crs), .sel(rs));
  Multiplexer #(.select(5), .width(32), .enable("false")) multiplexer_2 (
    .in0(R0_q), .in1(R1_q), .in2(R2_q), .in3(R3_q), .in4(R4_q), .in5(R5_q), .in6(R6_q), .in7(R7_q),
    .in8(R8_q), .in9(R9_q), .in10(R10_q), .in11(R11_q), .in12(R12_q), .in13(R13_q), .in14(R14_q),
    .in15(R15_q), .in16(R16_q), .in17(R17_q), .in18(R18_q), .in19(R19_q), .in20(R20_q), .in21(R21_q),
    .in22(R22_q), .in23(R23_q), .in24(R24_q), .in25(R25_q), .in26(R26_q), .in27(R27_q), .in28(R28_q),
    .in29(R29_q), .in30(R30_q), .in31(R31_q), .out(crd), .sel(rt));

  // Notes on the sheet:
  //   B86524 - Gabriel Revillat Zeledón
  //   NOTA: Hace falta hacer un AND entre cada salida del demultiplexor y un pin de un bit de entrada.
endmodule
